// Logisim project binarysearch.circ as structural Verilog: 3 circuits, main circuit main
module main (
  input  [4:0] Number_to_be_searched,
  output Not_Present,
  output Number_Found,
  output [3:0] Location,
  output [3:0] Current_Address_being_checked,
  output [4:0] Current_number_being_checked
);

  wire and_3_out, clock_out, comparator_1_eq, comparator_1_gt;
  wire [3:0] adder_1_out, adder_2_out, and_1_out, and_2_out, Front_Address_q, Rear_Address_q,
       subtractor_1_out;
  wire [3:3] comparator_2_gt, comparator_2_lt;
  wire [4:4] adder_1_cout, shifter_1_out;

  Clock clock (.out(clock_out));
  Register #(.width(4)) Front_Address (
    .D(and_1_out), .en(comparator_2_lt[3]), .Q(Front_Address_q), .clk(clock_out));  // open: clr
  assign and_1_out = {4{comparator_2_lt[3]}} & adder_2_out;  // AND_Gate and_1, 4 bits wide
  Register #(.width(4)) Rear_Address (
    .D(and_2_out), .en(comparator_2_gt[3]), .Q(Rear_Address_q), .clk(clock_out));  // open: clr
  Comparator #(.width(4), .mode("unsigned")) comparator_1 (
    .a(Front_Address_q), .b(Rear_Address_q), .gt(comparator_1_gt), .eq(comparator_1_eq));  // open: lt
  assign and_2_out = {4{comparator_2_gt[3]}} & subtractor_1_out;  // AND_Gate and_2, 4 bits wide
  Adder #(.width(4)) adder_1 (
    .a(Front_Address_q), .b(Rear_Address_q), .out(adder_1_out), .cout(adder_1_cout[4]));  // open: cin
  Adder #(.width(4)) adder_2 (.a(Current_Address_being_checked), .b(4'b0001), .out(adder_2_out));  // open: cin, cout
  and and_3 (and_3_out, comparator_1_eq, ~Number_Found);  // AND_Gate
  Shifter #(.width(5), .shift("lr")) shifter_1 (
    .in({adder_1_cout[4], adder_1_out}), .\dist (3'b001),
    .out({shifter_1_out[4], Current_Address_being_checked}));
  or or_1 (Not_Present, comparator_1_gt, and_3_out);
  Subtractor #(.width(4)) subtractor_1 (
    .a(Current_Address_being_checked), .b(4'b0001), .out(subtractor_1_out));  // open: bin, bout
  mem Memory (.in_1(Current_Address_being_checked), .out_2(Current_number_being_checked));
  Comparator #(.width(5), .mode("unsigned")) comparator_2 (
    .a(Current_number_being_checked), .b(Number_to_be_searched), .gt(comparator_2_gt[3]), .eq(Number_Found),
    .lt(comparator_2_lt[3]));
  assign Location = {4{Number_Found}} & Current_Address_being_checked;  // AND_Gate and_4, 4 bits wide
  Hex_Digit_Display hex_digit_display_1 (.value(Location));  // open: dp

  // Notes on the sheet:
  //   Right shift
  //   Location
endmodule

module mem (
  input  [3:0] in_1,
  output [4:0] out_2
);

  Multiplexer #(.select(4), .width(5)) multiplexer_1 (
    .in0({5{1'b0}}), .in1(5'b00001), .in2(5'b00100), .in3(5'b00110), .in4(5'b00111), .in5(5'b01001),
    .in6(5'b01010), .in7(5'b01100), .in8(5'b01111), .in9(5'b10000), .in10(5'b10100), .in11(5'b10110),
    .in12(5'b11001), .in13(5'b11010), .in14(5'b11100), .in15({5{1'b1}}), .out(out_2), .sel(in_1));  // open: en

  // Notes on the sheet:
  //   Numbers in hexadecimal
endmodule

module _6address (
  input  [4:0] Number_to_be_searched,
  output [4:0] Current_number,
  output Number_Found,
  output Not_Present
);

  wire and_1_out, and_2_out, and_3_out, and_4_out, and_5_out, and_6_out, and_7_out, and_9_out, and_10_out,
       clock_1_out, comparator_1_gt, comparator_1_lt, i0, i1, or_1_out, or_2_out, or_3_out, s0, s1, s2;

  and and_1 (and_1_out, s1, ~i0, i1);  // AND_Gate
  Clock clock_1 (.out(clock_1_out));
  or or_1 (or_1_out, s0, and_1_out);
  and and_2 (and_2_out, s0, ~i0, i1);  // AND_Gate
  and and_3 (and_3_out, i0, s1);
  and and_4 (and_4_out, ~s1, ~i0, i1);  // AND_Gate
  D_Flip_Flop d_ff_1 (.clk(clock_1_out), .D(or_1_out), .Q(s0));  // open: Qn, preset, en, reset
  or or_2 (or_2_out, and_2_out, and_3_out, and_4_out);
  mem Memory (.in_1({1'b0, s0, s1, s2}), .out_2(Current_number));
  D_Flip_Flop d_ff_2 (.clk(clock_1_out), .D(or_2_out), .Q(s1));  // open: Qn, preset, en, reset
  and and_5 (and_5_out, s1, ~i0);  // AND_Gate
  and and_6 (and_6_out, i0, s2);
  D_Flip_Flop d_ff_3 (.clk(clock_1_out), .D(or_3_out), .Q(s2));  // open: Qn, preset, en, reset
  or or_3 (or_3_out, and_5_out, and_6_out);
  Comparator #(.width(5), .mode("unsigned")) comparator_1 (
    .a(Current_number), .b(Number_to_be_searched), .gt(comparator_1_gt), .eq(Number_Found),
    .lt(comparator_1_lt));
  and and_7 (and_7_out, ~s2, ~i0);  // AND_Gate
  and and_8 (i0, ~comparator_1_gt, Number_Found, ~comparator_1_lt);  // AND_Gate
  and and_9 (and_9_out, ~comparator_1_gt, ~Number_Found, comparator_1_lt);  // AND_Gate
  or or_4 (Not_Present, and_7_out, and_10_out);
  and and_10 (and_10_out, s1, s0, ~i0);  // AND_Gate
  or or_5 (i1, i0, and_9_out);

  // Notes on the sheet:
  //   Location Addresses
endmodule
